# Fritzing sketch SusickaMasa (saved by Fritzing 0.9.2b)
breadboards: 1

parts:
  Load_Cell1 = Load Cell - Red/white/black/green
  Part1 = HX711 Weighing Sensor Module
  Load_Cell2 = Load Cell - Red/white/black/green
  Part2 = HX711 Weighing Sensor Module
  Load_Cell3 = Load Cell - Red/white/black/green
  Part3 = HX711 Weighing Sensor Module
  Load_Cell4 = Load Cell - Red/white/black/green
  Part4 = HX711 Weighing Sensor Module
  Součástka1 = Arduino Mega 2560 (Rev3)
  RHT1 = Humidity and Temperature Sensor RHT03
  R1 = Resistor [tolerance=±5% resistance=1k package=THT]
  LED1 = RGB LED (com. cathode, rgb) [package="5 mm [THT]"]

nets:
  N1: Load_Cell1.wire1, Part1.E+
  N2: Load_Cell1.wire2, Part1.A+
  N3: Load_Cell1.wire3, Part1.E-
  N4: Load_Cell1.wire4, Part1.A-
  VCC: Part1.VCC, Part2.VCC, Part3.VCC, Part4.VCC, Součástka1.5V, RHT1.Vcc
  GND: Part1.GND, Part2.GND, Part3.GND, Part4.GND, Součástka1.GND, RHT1.GND_1, LED1.common_cathode
  N5: Part1.DO/RX, Součástka1.D53
  N6: Part1.CK/TX, Součástka1.D51
  N7: Load_Cell2.wire1, Part2.E+
  N8: Load_Cell2.wire2, Part2.A+
  N9: Load_Cell2.wire3, Part2.E-
  N10: Load_Cell2.wire4, Part2.A-
  N11: Part2.DO/RX, Součástka1.D49
  N12: Part2.CK/TX, Součástka1.D47
  N13: Load_Cell3.wire1, Part3.E+
  N14: Load_Cell3.wire2, Part3.A+
  N15: Load_Cell3.wire3, Part3.E-
  N16: Load_Cell3.wire4, Part3.A-
  N17: Part3.DO/RX, Součástka1.D45
  N18: Part3.CK/TX, Součástka1.D43
  N19: Load_Cell4.wire1, Part4.E+
  N20: Load_Cell4.wire2, Part4.A+
  N21: Load_Cell4.wire3, Part4.E-
  N22: Load_Cell4.wire4, Part4.A-
  N23: Part4.DO/RX, Součástka1.D41
  N24: Part4.CK/TX, Součástka1.D39
  N25: Součástka1.D37, RHT1.Data-signal, R1.Pin_0

custom parts:
  Load Cell - Red/white/black/green: A rectangle load cell/weighting pressure Sensor with four wires - Red, white, black, green. Normally corresponding with E+, E-, A+, A- respectively.
  HX711 Weighing Sensor Module: HX711 is a precision 24-bit analog-to-digital converter (ADC) designed for weigh scales and industrial control applications to interface directly with a bridge sensor.
